// Logisim project full_adder.circ as structural Verilog: 3 circuits, main circuit main
module main (
  input  A1,
  input  B1,
  input  A0,
  input  B0,
  output S1,
  output Cout,
  output S0
);

  wire ha_1_c;

  FA fa_1 (.Cin(ha_1_c), .A(A1), .B(B1), .S(S1), .Cout(Cout));
  HA ha_1 (.A(A0), .B(B0), .S(S0), .C(ha_1_c));
endmodule

module HA (
  input  A,
  input  B,
  output S,
  output C
);

  xor xor_1 (S, A, B);
  and and_1 (C, A, B);
endmodule

module FA (
  input  Cin,
  input  A,
  input  B,
  output S,
  output Cout
);

  wire ha_1_c, ha_1_s, ha_2_c;

  HA ha_1 (.A(A), .B(B), .S(ha_1_s), .C(ha_1_c));
  HA ha_2 (.A(Cin), .B(ha_1_s), .S(S), .C(ha_2_c));
  or or_1 (Cout, ha_2_c, ha_1_c);
endmodule
